// Logisim project Dragon_5.circ as structural Verilog: 5 circuits, main circuit main
module main (
);

  Pipeline_ID ID_Stage ();  // open: Inst_Cache_1_IN, Inst_Cache_2_IN, WE, Inst_1_out, Inst_2_out
  Register_File reg_file ();  // open: RegF_rst, RegF_WE, RegF_A1, RegF_A2, RegF_A3, RegF_WD, RegF_D1, RegF_D2
  ALU Arithmetic_logic_Unit ();  // open: ALU_OP_IN, ALU_A_IN, ALU_B_IN, ALU_FLAG_IN, ALU_RES_OUT, ALU_FLAG_OUT
endmodule

module ALU (
  input  [3:0] ALU_OP_IN,
  input  [15:0] ALU_A_IN,
  input  [15:0] ALU_B_IN,
  input  [15:0] ALU_FLAG_IN,
  output [15:0] ALU_RES_OUT,
  output [15:0] ALU_FLAG_OUT
);

  wire adder_1_cout, adder_2_cout, adder_3_cout;
  wire [15:0] adder_1_out;

  Pull_Resistor pull_resistor_1 (.node(ALU_RES_OUT));
  Adder #(.width(4)) adder_1 (
    .a(ALU_A_IN[3:0]), .b(ALU_B_IN[3:0]), .out(adder_1_out[3:0]), .cout(adder_1_cout));  // open: cin
  Adder #(.width(4)) adder_2 (
    .a(ALU_A_IN[7:4]), .b(ALU_B_IN[7:4]), .out(adder_1_out[7:4]), .cin(adder_1_cout), .cout(adder_2_cout));
  Adder #(.width(4)) adder_3 (
    .a(ALU_A_IN[11:8]), .b(ALU_B_IN[11:8]), .out(adder_1_out[11:8]), .cin(adder_2_cout), .cout(adder_3_cout));
  Adder #(.width(4)) adder_4 (
    .a(ALU_A_IN[15:12]), .b(ALU_B_IN[15:12]), .out(adder_1_out[15:12]), .cin(adder_3_cout));  // open: cout
  Controlled_Buffer #(.width(16)) controlled_buffer_1 (.in(adder_1_out));  // open: out, en

  // Other names for the same wires on the sheet: ALU_A[15:0] = ALU_A_IN; ALU_B[15:0] = ALU_B_IN;
  //   ALU_OP[3:0] = ALU_OP_IN; ALU_RES[15:0] = ALU_RES_OUT
endmodule

module Register_File (
  input  RegF_rst,
  input  RegF_WE,
  input  [4:0] RegF_A1,
  input  [4:0] RegF_A2,
  input  [4:0] RegF_A3,
  input  [15:0] RegF_WD,
  output [15:0] RegF_D1,
  output [15:0] RegF_D2
);

  wire clock_1_out;
  wire [4:0] multiplexer_1_out, multiplexer_2_out;
  wire [15:0] bit_extender_1_out, bit_extender_2_out;

  assign bit_extender_1_out = {{11{1'b0}}, multiplexer_1_out};  // Bit_Extender bit_extender_1
  Multiplexer #(.width(5)) multiplexer_1 (.in0(RegF_A1), .in1(RegF_A3), .out(multiplexer_1_out), .sel(RegF_WE));
  Clock clock_1 (.out(clock_1_out));
  assign bit_extender_2_out = {{11{1'b0}}, multiplexer_2_out};  // Bit_Extender bit_extender_2
  Multiplexer #(.width(5)) multiplexer_2 (.in0(RegF_A2), .in1(RegF_A3), .out(multiplexer_2_out), .sel(RegF_WE));
  RAM #(.addrWidth(16), .dataWidth(16)) ram_1 (
    .addr(bit_extender_1_out), .we(RegF_WE), .oe(1'b1), .clk(clock_1_out), .din(RegF_WD), .dout(RegF_D1));
  RAM #(.addrWidth(16), .dataWidth(16)) ram_2 (
    .addr(bit_extender_2_out), .we(RegF_WE), .oe(1'b1), .clk(clock_1_out), .din(RegF_WD), .dout(RegF_D2));

  // Other names for the same wires on the sheet: RegF_bus_A[15:0] = RegF_D1; RegF_bus_B[15:0] = RegF_D2;
  //   RegF_D_in[15:0] = RegF_WD; RegF_reset = RegF_rst
endmodule

module Pipeline_ID (
  input  WE,
  input  [15:0] Inst_Cache_1_IN,
  input  [15:0] Inst_Cache_2_IN,
  output [15:0] Inst_1_out,
  output [15:0] Inst_2_out
);

  wire reset, undriven;

  Register #(.width(16)) register_1 (.D(Inst_Cache_1_IN), .en(undriven), .clk(WE), .Q(Inst_1_out), .clr(reset));
  Clock clock_1 (.out(WE));
  Register #(.width(16)) register_2 (.D(Inst_Cache_2_IN), .en(undriven), .clk(WE), .Q(Inst_2_out), .clr(reset));
endmodule

module Instruction_Cache (
  input  [15:0] InstC_A,
  input  [7:0] InstC_MBR,
  input  [15:0] InstC_RAM_DATA,
  input  InstC_CU_Acc,
  input  InstC_reset,
  input  InstC_lookup,
  output [15:0] InstC_RAM_A_BUS,
  output [7:0] InstC_RAM_MBR,
  output [15:0] InstC_Data_Out,
  output InstC_CU_Stall_Req
);

  wire adder_1_cout, adder_2_cout, and_1_out, and_2_out, and_3_out, clock_1_out, clock_2_out, clock_3_out,
       comparator_1_eq, comparator_1_gt, comparator_1_lt, counter_1_carry, not_1_out, not_2_out, or_1_out,
       or_2_out, or_4_out, or_5_out, s_r_ff_1_qn, undriven, undriven_2, undriven_3, undriven_4;
  wire [3:0] counter_1_q;
  wire [7:0] intr_cache_tag_sram_dout, multiplexer_2_out_2;
  wire [7:7] multiplexer_2_out;
  wire [15:0] bit_extender_1_out, multiplexer_1_out;

  and and_1 (and_1_out, counter_1_carry, clock_2_out);
  Counter #(.max('hf), .width(4)) counter_1 (
    .clr(or_1_out), .load(1'b0), .up(1'b1), .count(InstC_CU_Acc), .clk(clock_1_out), .D(4'b0000),
    .carry(counter_1_carry), .Q(counter_1_q));
  or or_1 (or_1_out, InstC_reset, and_1_out);
  Clock clock_1 (.out(clock_1_out));
  Clock clock_2 (.out(clock_2_out));
  assign bit_extender_1_out = {{12{1'b0}}, counter_1_q};  // Bit_Extender bit_extender_1
  S_R_Flip_Flop s_r_ff_1 (
    .S(undriven_2), .R(undriven_3), .clk(undriven_4), .Q(InstC_CU_Stall_Req), .reset(or_2_out),
    .Qn(s_r_ff_1_qn), .preset(and_2_out));
  // NoConnect on undriven_2
  // NoConnect on undriven_3
  // NoConnect on undriven_4
  or or_2 (or_2_out, counter_1_carry, InstC_reset);
  // NoConnect on undriven
  Adder #(.width(16)) adder_1 (
    .a(InstC_A), .b(bit_extender_1_out), .out(InstC_RAM_A_BUS), .cin(undriven), .cout(adder_1_cout));
  Adder adder_2 (.a(InstC_MBR), .b({8{1'b0}}), .out(InstC_RAM_MBR), .cin(adder_1_cout), .cout(adder_2_cout));
  // NoConnect on adder_2_cout
  Multiplexer #(.width(16)) multiplexer_1 (
    .in0(InstC_A), .in1(InstC_RAM_A_BUS), .out(multiplexer_1_out), .sel(InstC_CU_Stall_Req));
  // NoConnect on s_r_ff_1_qn
  not not_1 (not_1_out, and_3_out);
  and and_2 (and_2_out, not_1_out, InstC_lookup);
  Multiplexer #(.width(8)) multiplexer_2 (
    .in0(InstC_MBR), .in1(InstC_RAM_MBR), .out({multiplexer_2_out[7], multiplexer_2_out_2[6:0]}),
    .sel(InstC_CU_Stall_Req));
  // NoConnect on multiplexer_2_out[7]
  or or_3 (multiplexer_2_out_2[7], 1'b1, or_4_out);
  buf or_4 (or_4_out, InstC_CU_Acc);  // OR_Gate
  Clock clock_3 (.out(clock_3_out));
  or or_5 (or_5_out, counter_1_carry, and_3_out);
  not not_2 (not_2_out, clock_3_out);
  RAM #(.addrWidth(16), .asyncread("true"), .dataWidth(16)) istr_cache_data_sram (
    .addr(multiplexer_1_out), .we(or_4_out), .oe(or_5_out), .clk(not_2_out), .din(InstC_RAM_DATA),
    .dout(InstC_Data_Out));
  RAM #(.addrWidth(16), .asyncread("true")) intr_cache_tag_sram (
    .addr(multiplexer_1_out), .we(or_4_out), .oe(1'b1), .clk(not_2_out), .din(multiplexer_2_out_2),
    .dout(intr_cache_tag_sram_dout));
  // NoConnect on InstC_MBR[7]
  // NoConnect on comparator_1_gt
  Comparator #(.mode("unsigned"), .width(7)) comparator_1 (
    .a(intr_cache_tag_sram_dout[6:0]), .b(InstC_MBR[6:0]), .gt(comparator_1_gt), .eq(comparator_1_eq),
    .lt(comparator_1_lt));
  // NoConnect on comparator_1_lt
  and and_3 (and_3_out, comparator_1_eq, intr_cache_tag_sram_dout[7]);

  // Notes on the sheet:
  //   tag
  //   valid bit
  //   index + offset
  //   data
  //   tag + meta data
  //   7-bit tag | 1 valid bit
  //   tag
  //   valid
  //   Cache Hit
endmodule
